# Fritzing sketch scheme (saved by Fritzing 0.9.3b)
breadboards: 1

parts:
  R1 = Photocell (LDR) [package=THT]
  DHT11_1 = DHT11 module
  R2 = Resistor [tolerance=±5% resistance=10k package="1206 [SMD]"]
  U1 = NodeMCU V1.0

nets:
  VCC: R1.pin_0, DHT11_1.VCC, U1.3V3
  N1: R1.pin_1, R2.Pin_1, U1.A0
  GND: DHT11_1.GND, R2.Pin_0, U1.GND
  N2: DHT11_1.DATA, U1.D5

custom parts:
  DHT11 module: DHT11 black pcb module
  NodeMCU V1.0: ESP8266 based NodeMCU
